# Fritzing sketch 0_2button_seven_segments (saved by Fritzing 0.9.3b)
breadboards: 1

parts:
  元件1 = Adafruit T-Cobbler Plus [part_number="Adafruit #1989 and #2028"]
  R1 = Resistor [tolerance=±5% resistance=220 package=THT]
  LED1 = RGB LED (com. cathode, rgb) [package="5 mm [THT]"]
  R2 = Resistor [tolerance=±5% resistance=220 package=THT]
  R3 = Resistor [tolerance=±5% resistance=220 package=THT]
  S1 = Pushbutton [package="[THT]"]

nets:
  N1: 元件1.GND, LED1.common_cathode, S1.Pin_1, S1.Pin_2
  N2: 元件1.GPIO17, R1.Pin_0
  N3: 元件1.GPIO27, R2.Pin_0
  N4: 元件1.GPIO22, R3.Pin_0
  N5: 元件1.GPIO18, S1.Pin_3, S1.Pin_4
  N6: R1.Pin_1, LED1.red_anode
  N7: LED1.green_anode, R2.Pin_1
  N8: LED1.blue_anode, R3.Pin_1

custom parts:
  Adafruit T-Cobbler Plus: The Raspberry Pi has landed on the Maker World like a 40-GPIO pinned, quad-USB ported, credit card sized bomb of DIY joy. And while you can use most of our great Model B accessories by hooking up our downgrade cable, its probably a good time to upgrade your set up and accessorize using all of the 40 pins. That's why we now carry the Assembled Adafruit Pi T-Cobbler Plus - Breakout + Cable for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
